# Fritzing sketch Receiver (saved by Fritzing 0.9.10b)

parts:
  Power_plug1 = Power plug [mn=12V]
  L298N1 = L298N DC motor driver
  DC1 = DC_DC_XL4016 [mn="12V -> 6V" package=board_screw]
  Part1 = NRF24L01+ Breakout Board
  Part2 = Arduino Uno (Rev3) - ICSP
  M1 = DC Motor [voltage_(max)=3.3V voltage_(min)=3V]
  M2 = DC Motor [voltage_(max)=3.3V voltage_(min)=3V]

nets:
  GND: Power_plug1.GND, DC1.IN-, Part1.GND, Part2.GND
  VCC: Power_plug1.VCC, DC1.IN+, Part2.VIN
  N1: L298N1.OUT1, M1.pin_2
  N2: L298N1.OUT2, M1.pin_1
  N3: L298N1.OUT3, M2.pin_2
  N4: L298N1.OUT4, M2.pin_1
  N5: L298N1.12V, DC1.OUT+
  N6: L298N1.GND, DC1.OUT-
  N7: L298N1.5V#9, L298N1.ENA
  N8: L298N1.5V#10, L298N1.ENB
  N9: L298N1.IN1, Part2.D7
  N10: L298N1.IN2, Part2.D6_PWM
  N11: L298N1.IN3, Part2.D5_PWM
  N12: L298N1.IN4, Part2.D4
  VCC_2: Part1.VCC, Part2.3V3
  N13: Part1.CE, Part2.D9_PWM
  N14: Part1.CS, Part2.D8
  N15: Part1.SCK, Part2.D13/SCK
  N16: Part1.MOSI, Part2.D11_PWM/MOSI
  N17: Part1.MISO, Part2.ICSP_MISO, Part2.D12/MISO

custom parts:
  L298N DC motor driver: 2x DC motor driver with 78M05 positive voltage regulator (7..35 V) L298N: max 46 V, 2 A Set 5 V Enable jumper to enable 5 V regultor (needed for the L298N) and +5 V output at screw terminal or supply external +5 V at screw terminal Set ENA and/or ENB to +5 V to enable motor permanently or supply ENA and/or ENB with PWM signal IN1 and IN2 set rotation directory for motor A (OUT1/OUT2) IN2 and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
