# Fritzing sketch Transmitter (saved by Fritzing 0.9.10b)

parts:
  Part1 = Arduino Nano (Rev3.0)
  Part2 = Thumb Joystick
  Part3 = NRF24L01+ Breakout Board
  S1 = Round Pushbutton
  VCC1 = Battery block 9V
  C1 = Electrolytic Capacitor [capacitance=100µF voltage=16V package="100 mil [THT, electrolytic]"]

nets:
  GND: Part1.GND, Part3.GND, VCC1.-, C1.-
  N1: Part1.D8, Part3.CS
  N2: Part1.D9, Part3.CE
  N3: Part1.D11/MOSI, Part3.MOSI
  N4: Part1.D12/MISO, Part3.MISO
  N5: Part1.VIN, S1.leg1
  5V: Part1.5V, Part2.VCC
  N6: Part1.A1, Part2.HORZ
  N7: Part1.A0, Part2.VERT
  3V3: Part1.3V3, Part3.VCC, C1.+
  N8: Part1.D13/SCK, Part3.SCK
  N9: S1.leg0, VCC1.+
